// Logisim project IT012_Lab01_25520174.circ as structural Verilog: 5 circuits, main circuit TN5
module TN5 (
  input  A,
  input  B,
  input  C,
  output F1,
  output F
);

  wire and_1_out, xor_1_out, xor_2_out;

  and and_1 (and_1_out, C, B, A);
  ExactlyOne xor_1 (.out(xor_1_out), .in1(A), .in2(B), .in3(C));
  xor xor_2 (xor_2_out, A, B);
  or or_1 (F1, and_1_out, xor_1_out);
  xor xor_3 (F, xor_2_out, C);
endmodule

module TN1 (
  input  A,
  input  A_2,
  input  A_3,
  input  B,
  input  B_2,
  input  A_4,
  input  C,
  input  B_3,
  input  A_5,
  input  A_6,
  input  B_4,
  input  B_5,
  input  in_13,
  input  A_7,
  input  A_8,
  input  B_6,
  input  B_7,
  input  A_9,
  input  C_2,
  input  B_8,
  input  A_10,
  input  B_9,
  output A_prime,
  output AND,
  output XOR3,
  output OR,
  output A_11,
  output NAND3,
  output B_10,
  output CHAIN,
  output XOR,
  output XNOR
);

  wire X_out;

  not not_1 (A_prime, A);
  and and_1 (AND, A_2, B);
  or or_1 (OR, A_4, B_3);
  nand nand_1 (A_11, A_6, B_5);
  nor nor_1 (B_10, A_7, B_6);
  xor xor_1 (XOR, A_9, B_8);
  xnor xnor_1 (XNOR, A_10, B_9);
  ExactlyOne xor_2 (.out(XOR3), .in1(A_3), .in2(B_2), .in3(C));
  nand nand_2 (NAND3, A_5, B_4, in_13);
  nand X (X_out, A_8, B_7);
  nand Y (CHAIN, X_out, C_2);

  // Notes on the sheet:
  //   NAND
  //   NOR
endmodule

module TN2 (
  input  X,
  input  Y,
  input  Z,
  output EQ1,
  output EQ2,
  output EQ3,
  output EQ4,
  output EQ5
);

  wire and_1_out, and_2_out, and_3_out, and_4_out, and_5_out, and_6_out, nand_1_out, nor_1_out, not_1_out,
       not_2_out, not_3_out, or_1_out, or_2_out, or_3_out, or_4_out, or_5_out, or_6_out;

  not not_1 (not_1_out, X);
  not not_2 (not_2_out, Y);
  not not_3 (not_3_out, Z);
  and and_1 (and_1_out, not_1_out, not_2_out);
  and and_2 (and_2_out, not_1_out, not_2_out);
  and and_3 (and_3_out, Y, Z);
  or or_1 (or_1_out, X, Y);
  or or_2 (or_2_out, X, Z);
  and and_4 (and_4_out, not_1_out, Y);
  and and_5 (and_5_out, not_1_out, Y);
  or or_3 (or_3_out, X, Y);
  nor nor_1 (nor_1_out, X, Y);
  nand nand_1 (nand_1_out, X, Y);
  or or_4 (or_4_out, X, and_4_out);
  or or_5 (or_5_out, X, and_5_out);
  xnor xnor_1 (EQ1, nor_1_out, and_1_out);
  xnor xnor_2 (EQ2, nand_1_out, and_2_out);
  or or_6 (or_6_out, X, and_3_out);
  and and_6 (and_6_out, or_1_out, or_2_out);
  xnor xnor_3 (EQ3, or_6_out, and_6_out);
  xnor xnor_4 (EQ4, or_4_out, X);
  xnor xnor_5 (EQ5, or_5_out, or_3_out);
endmodule

module TN3 (
  input  A,
  input  B,
  input  C,
  input  D,
  output F
);

  wire and_1_out, and_2_out, and_3_out, and_4_out, and_5_out, and_6_out, not_1_out, not_2_out, not_3_out,
       not_4_out, or_1_out;

  not not_1 (not_1_out, A);
  not not_2 (not_2_out, B);
  not not_3 (not_3_out, C);
  not not_4 (not_4_out, D);
  and and_1 (and_1_out, not_1_out, not_2_out, C, not_4_out);
  and and_2 (and_2_out, not_1_out, not_2_out, C, D);
  and and_3 (and_3_out, not_1_out, B, not_3_out, D);
  and and_4 (and_4_out, not_1_out, B, C, D);
  and and_5 (and_5_out, A, not_2_out, C, D);
  and and_6 (and_6_out, A, B, not_3_out, D);
  or or_1 (or_1_out, and_1_out, and_2_out);
  or or_2 (F, or_1_out, and_3_out, and_4_out, and_5_out, and_6_out);
endmodule

module TN4 (
  input  A,
  input  B,
  input  C,
  input  D,
  output EQ1,
  output EQ2
);

  wire and_1_out, and_2_out, and_3_out, and_4_out, and_5_out, and_6_out, and_7_out, and_8_out, and_9_out,
       and_10_out, and_11_out, not_1_out, not_2_out, not_3_out, not_4_out, or_1_out, or_2_out, or_3_out,
       or_4_out, or_5_out, or_6_out, or_7_out;

  not not_1 (not_1_out, A);
  not not_2 (not_2_out, B);
  not not_3 (not_3_out, C);
  not not_4 (not_4_out, D);
  and and_1 (and_1_out, not_1_out, not_2_out, C, not_4_out, not_1_out);
  and and_2 (and_2_out, not_1_out, not_2_out, C, D);
  and and_3 (and_3_out, not_1_out, B, not_3_out, D);
  and and_4 (and_4_out, not_1_out, B, C, D);
  and and_5 (and_5_out, A, not_2_out, C, D);
  and and_6 (and_6_out, A, B, not_3_out, D);
  and and_7 (and_7_out, B, not_3_out, D);
  and and_8 (and_8_out, not_1_out, C, D);
  and and_9 (and_9_out, not_2_out, C, D);
  and and_10 (and_10_out, not_1_out, not_2_out, C);
  or or_1 (or_1_out, B, C);
  or or_2 (or_2_out, not_2_out, D);
  or or_3 (or_3_out, not_1_out, D);
  or or_4 (or_4_out, not_1_out, not_2_out, not_3_out);
  or or_5 (or_5_out, and_1_out, and_2_out);
  and and_11 (and_11_out, or_1_out, or_2_out, or_3_out, or_4_out);
  or or_6 (or_6_out, and_7_out, and_8_out, and_9_out, and_10_out);
  or or_7 (or_7_out, or_5_out, and_3_out, and_4_out, and_5_out, and_6_out);
  xnor xnor_1 (EQ1, or_7_out, or_6_out);
  xnor xnor_2 (EQ2, or_7_out, and_11_out);

  // Notes on the sheet:
  //   F_sop
  //   F_pos
  //   F_can
endmodule
